// Logisim project cpu.circ as structural Verilog: 2 circuits, main circuit main
module main (
  input  [31:0] INSTRUCTION,
  input  CLOCK,
  output [31:0] FETCH_ADDRESS,
  output [31:0] s0_Value,
  output [31:0] s1_Value,
  output [31:0] t0_Value,
  output [31:0] t1_Value,
  output [31:0] a0_Value,
  output [31:0] ra_Value,
  output [31:0] sp_Value
);

  wire Add, addASel, addBSel, Addi, addiASel, addiMemRW, addiPCSel, addMemRW, addPCSel, And, andASel,
       andBSel, Andi, andiASel, andiBSel, andiMemRW, andiPCSel, andMemRW, andPCSel, ASel, Beq, Blt, Bltu,
       brLT, BSel, comparator_1_eq, comparator_1_lt, comparator_2_eq, comparator_2_lt, Div, divASel, divBSel,
       divMemRW, divPCSel, Jal, Jalr, lbMemRW, lbPCSel, Lh, lhASel, lhMemRW, lhPCSel, Lui, Lw, lwASel,
       lwMemRW, lwPCSel, MEM_p1, MEM_p2, MEM_p4, MEM_p10, MemRW, Mul, mulASel, mulBSel, MulH, mulhASel,
       mulhBSel, mulhMemRW, mulhPCSel, mulMemRW, mulPCSel, NegSel, not_52_out, not_53_out, not_54_out,
       not_55_out, not_56_out, not_57_out, not_58_out, not_85_out, not_89_out, not_93_out, Or, orASel,
       orBSel, Ori, oriASel, oriBSel, oriMemRW, oriPCSel, orMemRW, orPCSel, PCSel, RegWEn, Rem, remASel,
       remBSel, remMemRW, remPCSel, Sll, sllASel, sllBSel, Slli, slliASel, slliMemRW, slliPCSel, sllMemRW,
       sllPCSel, Slt, sltASel, sltBSel, Slti, sltiASel, sltiBSel, sltiMemRW, sltiPCSel, sltMemRW, sltPCSel,
       Srl, srlASel, srlBSel, Srli, srliASel, srliBSel, srliMemRW, srliPCSel, srlMemRW, srlPCSel, subASel,
       subBSel, subMemRW, subPCSel, Sw, Xor, xorASel, xorBSel, Xori, xoriASel, xoriBSel, xoriMemRW,
       xoriPCSel, xorMemRW, xorPCSel;
  wire [1:0] addiWBSel, addWBSel, andiWBSel, andWBSel, bit_extender_50_out, bit_extender_52_out,
       bit_extender_56_out, divWBSel, lbWBSel, lhWBSel, lwWBSel, mulhWBSel, mulWBSel, oriWBSel, orWBSel,
       remWBSel, slliWBSel, sllWBSel, sltiWBSel, sltWBSel, srliWBSel, srlWBSel, subWBSel, WBSel, xoriWBSel,
       xorWBSel;
  wire [2:0] addiImmSel, andiImmSel, ImmSel, lbImmSel, lhImmSel, lwImmSel, oriImmSel, slliImmSel, sltiImmSel,
       srliImmSel, xoriImmSel;
  wire [3:0] addALUSel, addiALUSel, andALUSel, andiALUSel, bit_extender_1_out, bit_extender_3_out,
       bit_extender_5_out, bit_extender_7_out, bit_extender_9_out, bit_extender_11_out, bit_extender_13_out,
       bit_extender_15_out, bit_extender_19_out, bit_extender_21_out, bit_extender_23_out,
       bit_extender_29_out, bit_extender_32_out, bit_extender_35_out, bit_extender_38_out,
       bit_extender_44_out, bit_extender_47_out, bit_extender_54_out, bit_extender_55_out,
       bit_extender_58_out, divALUSel, lbALUSel, lhALUSel, lwALUSel, mulALUSel, mulhALUSel, orALUSel,
       oriALUSel, remALUSel, shifter_3_out, shifter_6_out, shifter_8_out, sllALUSel, slliALUSel, sltALUSel,
       sltiALUSel, srlALUSel, srliALUSel, subALUSel, xorALUSel, xoriALUSel;
  wire [24:0] demultiplexer_3_out1, Iimm, SBimm, Simm, Uimm, UJimm;
  wire [31:0] adder_1_out, bit_extender_25_out, bit_extender_26_out, bit_extender_27_out,
       bit_extender_28_out, demultiplexer_1_out0, demultiplexer_1_out1, demultiplexer_2_out0,
       demultiplexer_2_out1, immGen, main_2_result, MEM_p11, multiplexer_1_out, multiplexer_5_out,
       multiplexer_6_out, multiplexer_7_out, multiplexer_8_out, negator_1_out, R1, R2;

  Multiplexer #(.width(32)) multiplexer_1 (
    .in0(adder_1_out), .in1(main_2_result), .out(multiplexer_1_out), .sel(PCSel));  // open: en
  Register #(.width(32)) PC (.D(multiplexer_1_out), .Q(FETCH_ADDRESS), .clk(CLOCK));  // open: en, clr
  not not_1 (addPCSel, Add);
  not not_2 (addASel, Add);
  not not_3 (addBSel, Add);
  assign bit_extender_1_out = {{3{1'b0}}, Add};  // Bit_Extender bit_extender_1
  not not_4 (addMemRW, Add);
  assign addWBSel = {{1{1'b0}}, Add};  // Bit_Extender bit_extender_2
  not not_5 (mulPCSel, Mul);
  not not_6 (mulASel, Mul);
  not not_7 (mulBSel, Mul);
  assign bit_extender_3_out = {{3{1'b0}}, Mul};  // Bit_Extender bit_extender_3
  not not_8 (mulMemRW, Mul);
  assign mulWBSel = {{1{1'b0}}, Mul};  // Bit_Extender bit_extender_4
  not not_9 (subPCSel, NegSel);
  not not_10 (subASel, NegSel);
  not not_11 (subBSel, NegSel);
  assign bit_extender_5_out = {{3{1'b0}}, NegSel};  // Bit_Extender bit_extender_5
  not not_12 (subMemRW, NegSel);
  assign subWBSel = {{1{1'b0}}, NegSel};  // Bit_Extender bit_extender_6
  not not_13 (sllPCSel, Sll);
  not not_14 (sllASel, Sll);
  not not_15 (sllBSel, Sll);
  assign bit_extender_7_out = {{3{1'b0}}, Sll};  // Bit_Extender bit_extender_7
  not not_16 (sllMemRW, Sll);
  assign sllWBSel = {{1{1'b0}}, Sll};  // Bit_Extender bit_extender_8
  not not_17 (mulhPCSel, MulH);
  not not_18 (mulhASel, MulH);
  not not_19 (mulhBSel, MulH);
  assign bit_extender_9_out = {{3{1'b0}}, MulH};  // Bit_Extender bit_extender_9
  not not_20 (mulhMemRW, MulH);
  assign mulhWBSel = {{1{1'b0}}, MulH};  // Bit_Extender bit_extender_10
  not not_21 (sltPCSel, Slt);
  not not_22 (sltASel, Slt);
  not not_23 (sltBSel, Slt);
  assign bit_extender_11_out = {{3{1'b0}}, Slt};  // Bit_Extender bit_extender_11
  not not_24 (sltMemRW, Slt);
  assign sltWBSel = {{1{1'b0}}, Slt};  // Bit_Extender bit_extender_12
  not not_25 (xorPCSel, Xor);
  not not_26 (xorASel, Xor);
  not not_27 (xorBSel, Xor);
  assign bit_extender_13_out = {{3{1'b0}}, Xor};  // Bit_Extender bit_extender_13
  not not_28 (xorMemRW, Xor);
  assign xorWBSel = {{1{1'b0}}, Xor};  // Bit_Extender bit_extender_14
  not not_29 (divPCSel, Div);
  not not_30 (divASel, Div);
  not not_31 (divBSel, Div);
  assign bit_extender_15_out = {{3{1'b0}}, Div};  // Bit_Extender bit_extender_15
  not not_32 (divMemRW, Div);
  assign divWBSel = {{1{1'b0}}, Div};  // Bit_Extender bit_extender_16
  not not_33 (srlPCSel, Srl);
  not not_34 (srlASel, Srl);
  not not_35 (srlBSel, Srl);
  assign srlALUSel = {{3{1'b0}}, Srl};  // Bit_Extender bit_extender_17
  not not_36 (srlMemRW, Srl);
  assign srlWBSel = {{1{1'b0}}, Srl};  // Bit_Extender bit_extender_18
  not not_37 (orPCSel, Or);
  not not_38 (orASel, Or);
  not not_39 (orBSel, Or);
  assign bit_extender_19_out = {{3{1'b0}}, Or};  // Bit_Extender bit_extender_19
  not not_40 (orMemRW, Or);
  assign orWBSel = {{1{1'b0}}, Or};  // Bit_Extender bit_extender_20
  not not_41 (remPCSel, Rem);
  not not_42 (remASel, Rem);
  not not_43 (remBSel, Rem);
  assign bit_extender_21_out = {{3{1'b0}}, Rem};  // Bit_Extender bit_extender_21
  not not_44 (remMemRW, Rem);
  assign remWBSel = {{1{1'b0}}, Rem};  // Bit_Extender bit_extender_22
  not not_45 (andPCSel, And);
  not not_46 (andASel, And);
  not not_47 (andBSel, And);
  assign bit_extender_23_out = {{3{1'b0}}, And};  // Bit_Extender bit_extender_23
  not not_48 (andMemRW, And);
  assign andWBSel = {{1{1'b0}}, And};  // Bit_Extender bit_extender_24
  Adder #(.width(32)) adder_1 (.a(FETCH_ADDRESS), .b(32'h4), .out(adder_1_out));  // open: cin, cout
  Shifter #(.width(4)) shifter_1 (.in(bit_extender_1_out), .\dist (2'b01), .out(addALUSel));
  assign bit_extender_25_out = {{20{1'b0}}, Iimm[24:13]};  // Bit_Extender bit_extender_25
  assign bit_extender_26_out = {{20{1'b0}}, {Simm[24:18], Simm[4:0]}};  // Bit_Extender bit_extender_26
  assign bit_extender_27_out = {{19{1'b0}}, {SBimm[24], SBimm[0], SBimm[23:18], SBimm[4:1], 1'b0}};  // Bit_Extender bit_extender_27
  assign bit_extender_28_out = {{11{1'b0}}, {UJimm[24], UJimm[12:5], UJimm[13], UJimm[23:14], 1'b0}};  // Bit_Extender bit_extender_28
  assign mulALUSel = bit_extender_3_out | 4'b0111;  // OR_Gate or_1, 4 bits wide
  Shifter #(.width(4)) shifter_2 (.in(bit_extender_9_out), .\dist (2'b11), .out(mulhALUSel));
  Shifter #(.width(4)) shifter_3 (.in(bit_extender_11_out), .\dist (2'b01), .out(shifter_3_out));
  assign xorALUSel = bit_extender_13_out | 4'b0101;  // OR_Gate or_2, 4 bits wide
  assign divALUSel = bit_extender_15_out | 4'b1001;  // OR_Gate or_3, 4 bits wide
  assign andALUSel = bit_extender_23_out | 4'b0011;  // OR_Gate or_4, 4 bits wide
  Demultiplexer #(.width(32)) demultiplexer_1 (
    .out0(demultiplexer_1_out0), .out1(demultiplexer_1_out1), .in(R1), .en(Bltu));  // open: sel
  Demultiplexer #(.width(32)) demultiplexer_2 (
    .out0(demultiplexer_2_out0), .out1(demultiplexer_2_out1), .in(R2), .en(Bltu));  // open: sel
  Shifter #(.width(4)) shifter_4 (.in(bit_extender_5_out), .\dist (2'b01), .out(subALUSel));
  assign sllALUSel = bit_extender_7_out & 4'b0000;  // AND_Gate and_1, 4 bits wide
  assign sltALUSel = shifter_3_out | 4'b0110;  // OR_Gate or_5, 4 bits wide
  Shifter #(.width(4)) shifter_5 (.in(bit_extender_19_out), .\dist (2'b10), .out(orALUSel));
  Shifter #(.width(4)) shifter_6 (.in(bit_extender_21_out), .\dist (2'b01), .out(shifter_6_out));
  Demultiplexer #(.select(3), .width(25)) demultiplexer_3 (
    .out0(Iimm), .out1(demultiplexer_3_out1), .out2(SBimm), .out3(Uimm), .out4(UJimm),
    .in(INSTRUCTION[31:7]), .sel(ImmSel));  // open: out5, out6, out7, en
  Multiplexer #(.select(3), .width(32)) multiplexer_2 (
    .in0(bit_extender_25_out), .in1(bit_extender_26_out), .in2(bit_extender_27_out),
    .in3({Uimm[24:5], {12{1'b0}}}), .in4(bit_extender_28_out), .out(immGen), .sel(ImmSel));  // open: in5, in6, in7, en
  Comparator #(.width(32)) comparator_1 (
    .a(demultiplexer_1_out0), .b(demultiplexer_2_out0), .eq(comparator_1_eq), .lt(comparator_1_lt));  // open: gt
  Comparator #(.width(32), .mode("unsigned")) comparator_2 (
    .a(demultiplexer_1_out1), .b(demultiplexer_2_out1), .eq(comparator_2_eq), .lt(comparator_2_lt));  // open: gt
  assign remALUSel = shifter_6_out | 4'b1010;  // OR_Gate or_6, 4 bits wide
  Multiplexer multiplexer_3 (.in0(comparator_1_eq), .in1(comparator_2_eq), .out(Beq), .sel(Bltu));  // open: en
  Multiplexer multiplexer_4 (.in0(comparator_1_lt), .in1(comparator_2_lt), .out(brLT), .sel(Bltu));  // open: en
  not not_49 (addiPCSel, Addi);
  not not_50 (addiASel, Addi);
  assign bit_extender_29_out = {{3{1'b0}}, Addi};  // Bit_Extender bit_extender_29
  not not_51 (addiMemRW, Addi);
  assign addiWBSel = {{1{1'b0}}, Addi};  // Bit_Extender bit_extender_30
  not not_52 (not_52_out, Addi);
  not not_53 (not_53_out, Slli);
  not not_54 (not_54_out, Slti);
  not not_55 (not_55_out, Xori);
  not not_56 (not_56_out, Srli);
  not not_57 (not_57_out, Ori);
  not not_58 (not_58_out, Andi);
  regfile_main main_1 (
    .Read_Register_1__rs1(INSTRUCTION[19:15]), .Read_Register_2__rs2(INSTRUCTION[24:20]),
    .Write_Register__rd(INSTRUCTION[11:7]), .Write_Data(multiplexer_8_out), .Write_Enable(RegWEn),
    .Clock(CLOCK), .Read_Data_1(R1), .Read_Data_2(R2), .s1_Value(s1_Value), .t0_Value(t0_Value),
    .t1_Value(t1_Value), .a0_Value(a0_Value), .s0_Value(s0_Value), .ra_Value(ra_Value), .sp_Value(sp_Value));
  assign addiImmSel = {{2{1'b0}}, not_52_out};  // Bit_Extender bit_extender_31
  not not_59 (slliPCSel, Slli);
  not not_60 (slliASel, Slli);
  assign bit_extender_32_out = {{3{1'b0}}, Slli};  // Bit_Extender bit_extender_32
  not not_61 (slliMemRW, Slli);
  assign slliWBSel = {{1{1'b0}}, Slli};  // Bit_Extender bit_extender_33
  assign slliImmSel = {{2{1'b0}}, not_53_out};  // Bit_Extender bit_extender_34
  not not_62 (sltiPCSel, Slti);
  not not_63 (sltiASel, Slti);
  not not_64 (sltiBSel, Slti);
  assign bit_extender_35_out = {{3{1'b0}}, Slti};  // Bit_Extender bit_extender_35
  not not_65 (sltiMemRW, Slti);
  assign sltiWBSel = {{1{1'b0}}, Slti};  // Bit_Extender bit_extender_36
  assign sltiImmSel = {{2{1'b0}}, not_54_out};  // Bit_Extender bit_extender_37
  not not_66 (xoriPCSel, Xori);
  not not_67 (xoriASel, Xori);
  not not_68 (xoriBSel, Xori);
  assign bit_extender_38_out = {{3{1'b0}}, Xori};  // Bit_Extender bit_extender_38
  not not_69 (xoriMemRW, Xori);
  assign xoriWBSel = {{1{1'b0}}, Xori};  // Bit_Extender bit_extender_39
  assign xoriImmSel = {{2{1'b0}}, not_55_out};  // Bit_Extender bit_extender_40
  not not_70 (srliPCSel, Srli);
  not not_71 (srliASel, Srli);
  not not_72 (srliBSel, Srli);
  assign srliALUSel = {{3{1'b0}}, Srli};  // Bit_Extender bit_extender_41
  not not_73 (srliMemRW, Srli);
  assign srliWBSel = {{1{1'b0}}, Srli};  // Bit_Extender bit_extender_42
  assign srliImmSel = {{2{1'b0}}, not_56_out};  // Bit_Extender bit_extender_43
  not not_74 (oriPCSel, Ori);
  not not_75 (oriASel, Ori);
  not not_76 (oriBSel, Ori);
  assign bit_extender_44_out = {{3{1'b0}}, Ori};  // Bit_Extender bit_extender_44
  not not_77 (oriMemRW, Ori);
  assign oriWBSel = {{1{1'b0}}, Ori};  // Bit_Extender bit_extender_45
  assign oriImmSel = {{2{1'b0}}, not_57_out};  // Bit_Extender bit_extender_46
  not not_78 (andiPCSel, Andi);
  not not_79 (andiASel, Andi);
  not not_80 (andiBSel, Andi);
  assign bit_extender_47_out = {{3{1'b0}}, Andi};  // Bit_Extender bit_extender_47
  not not_81 (andiMemRW, Andi);
  assign andiWBSel = {{1{1'b0}}, Andi};  // Bit_Extender bit_extender_48
  assign andiImmSel = {{2{1'b0}}, not_58_out};  // Bit_Extender bit_extender_49
  Shifter #(.width(4)) shifter_7 (.in(bit_extender_29_out), .\dist (2'b01), .out(addiALUSel));
  Multiplexer #(.width(32)) multiplexer_5 (.in0(R2), .in1(immGen), .out(multiplexer_5_out), .sel(BSel));  // open: en
  assign slliALUSel = bit_extender_32_out & 4'b0000;  // AND_Gate and_2, 4 bits wide
  Shifter #(.width(4)) shifter_8 (.in(bit_extender_35_out), .\dist (2'b01), .out(shifter_8_out));
  assign xoriALUSel = bit_extender_38_out | 4'b0101;  // OR_Gate or_7, 4 bits wide
  Shifter #(.width(4)) shifter_9 (.in(bit_extender_44_out), .\dist (2'b10), .out(oriALUSel));
  assign andiALUSel = bit_extender_47_out | 4'b0011;  // OR_Gate or_8, 4 bits wide
  Multiplexer #(.width(32)) multiplexer_6 (
    .in0(R1), .in1(adder_1_out), .out(multiplexer_6_out), .sel(ASel));  // open: en
  Negator #(.width(32)) negator_1 (.in(multiplexer_5_out), .out(negator_1_out));
  control_unit Control_Unit (
    .Instruction(INSTRUCTION), .brEQ(Beq), .brLT(brLT), .JALRtype(Jalr), .JALtype(Jal), .LUItype(Lui),
    .BLTUtype(Bltu), .BLTtype(Blt), .BEQtype(Beq), .SWtype(Sw), .ANDItype(Andi), .ORItype(Ori),
    .SRLItype(Srli), .XORItype(Xori), .SLTItype(Slti), .SLLItype(Slli), .ADDItype(Addi), .LWtype(Lw),
    .LHtype(Lh), .LBtype(Addi), .ANDtype(And), .REMtype(Rem), .ORtype(Or), .SRLtype(Srl), .DIVtype(Div),
    .XORtype(Xor), .SLTtype(Slt), .MULHtype(MulH), .SLLtype(Sll), .SUBtype(NegSel), .MULtype(Mul),
    .ADDtype(Add));  // open: brEQ_2, brLT_2
  assign sltiALUSel = shifter_8_out | 4'b0110;  // OR_Gate or_9, 4 bits wide
  Multiplexer #(.width(32)) multiplexer_7 (
    .in0(multiplexer_5_out), .in1(negator_1_out), .out(multiplexer_7_out), .sel(NegSel));  // open: en
  alu_main main_2 (
    .Switch(4'b0001), .X(multiplexer_6_out), .Result(main_2_result), .Y(multiplexer_7_out));  // open: Equal
  not not_82 (lbPCSel, Addi);
  not not_83 (addiASel, Addi);
  not not_84 (lbMemRW, Addi);
  not not_85 (not_85_out, Addi);
  not not_86 (lwPCSel, Lw);
  not not_87 (lwASel, Lw);
  not not_88 (lwMemRW, Lw);
  not not_89 (not_89_out, Lw);
  // mem_main MEM: pin names not known; wires that end beside it: MEM_p1, MEM_p2, MEM_p2, MEM_p4, main_2_result, R2, MemRW, MEM_p4, CLOCK, MEM_p10, MEM_p11
  assign bit_extender_50_out = {{1{1'b0}}, Addi};  // Bit_Extender bit_extender_50
  Shifter #(.width(2)) shifter_10 (.in(bit_extender_50_out), .\dist (1'b1), .out(lbWBSel));
  assign lbImmSel = {{2{1'b0}}, not_85_out};  // Bit_Extender bit_extender_51
  assign bit_extender_52_out = {{1{1'b0}}, Lw};  // Bit_Extender bit_extender_52
  assign lwImmSel = {{2{1'b0}}, not_89_out};  // Bit_Extender bit_extender_53
  not not_90 (lhPCSel, Lh);
  not not_91 (lhASel, Lh);
  not not_92 (lhMemRW, Lh);
  not not_93 (not_93_out, Lh);
  assign bit_extender_54_out = {{3{1'b0}}, Addi};  // Bit_Extender bit_extender_54
  assign bit_extender_55_out = {{3{1'b0}}, Lw};  // Bit_Extender bit_extender_55
  Shifter #(.width(2)) shifter_11 (.in(bit_extender_52_out), .\dist (1'b1), .out(lwWBSel));
  assign bit_extender_56_out = {{1{1'b0}}, Lh};  // Bit_Extender bit_extender_56
  assign lhImmSel = {{2{1'b0}}, not_93_out};  // Bit_Extender bit_extender_57
  Multiplexer #(.select(2), .width(32)) multiplexer_8 (
    .in0(adder_1_out), .in1(main_2_result), .in2(MEM_p11), .out(multiplexer_8_out), .sel(WBSel));  // open: in3, en
  Shifter #(.width(4)) shifter_12 (.in(bit_extender_54_out), .\dist (2'b01), .out(lbALUSel));
  assign bit_extender_58_out = {{3{1'b0}}, Lh};  // Bit_Extender bit_extender_58
  Shifter #(.width(2)) shifter_13 (.in(bit_extender_56_out), .\dist (1'b1), .out(lhWBSel));
  Shifter #(.width(4)) shifter_14 (.in(bit_extender_55_out), .\dist (2'b01), .out(lwALUSel));
  Shifter #(.width(4)) shifter_15 (.in(bit_extender_58_out), .\dist (2'b01), .out(lhALUSel));

  // Other names for the same wires on the sheet: a0[31:0] = a0_Value; addRegWEn = Add; andiRegWEn = Andi;
  //   andRegWEn = And; brEQ = Beq; clk = CLOCK; divRegWEn = Div; fetch_addr[31:0] = FETCH_ADDRESS; addiBSel = Addi;
  //   addiRegWEn = Addi; Lb = Addi; lbRegWEn = Addi; lhBSel = Lh; lhRegWEn = Lh; lwBSel = Lw; lwRegWEn = Lw;
  //   mulhRegWEn = MulH; mulRegWEn = Mul; oriRegWEn = Ori; orRegWEn = Or; ra[31:0] = ra_Value; remRegWEn = Rem;
  //   s0[31:0] = s0_Value; s1[31:0] = s1_Value; slliBSel = Slli; slliRegWEn = Slli; sllRegWEn = Sll;
  //   sltiRegWEn = Slti; sltRegWEn = Slt; sp[31:0] = sp_Value; srliRegWEn = Srli; srlRegWEn = Srl; Sub = NegSel;
  //   subRegWEn = NegSel; t0[31:0] = t0_Value; t1[31:0] = t1_Value; xoriRegWEn = Xori; xorRegWEn = Xor

  // Notes on the sheet:
  //   Output
  //   These are outputs/inputs from run.circ
  //   Inputs
  //   These are DEBUG/TEST outputs from your circuit.
endmodule

module control_unit (
  input  [31:0] Instruction,
  input  brEQ,
  input  brLT,
  output JALRtype,
  output JALtype,
  output LUItype,
  output BLTUtype,
  output BLTtype,
  output BEQtype,
  output SWtype,
  output ANDItype,
  output ORItype,
  output SRLItype,
  output XORItype,
  output SLTItype,
  output SLLItype,
  output ADDItype,
  output LWtype,
  output LHtype,
  output LBtype,
  output ANDtype,
  output REMtype,
  output ORtype,
  output SRLtype,
  output DIVtype,
  output XORtype,
  output SLTtype,
  output MULHtype,
  output SLLtype,
  output SUBtype,
  output MULtype,
  output ADDtype,
  output brEQ_2,
  output brLT_2
);

  wire demultiplexer_1_out0, demultiplexer_1_out1, demultiplexer_2_out0, demultiplexer_3_out0,
       demultiplexer_4_out0, demultiplexer_4_out1, demultiplexer_5_out1, demultiplexer_6_out0,
       demultiplexer_9_out1, demultiplexer_11_out0, demultiplexer_11_out1, demultiplexer_12_out0,
       demultiplexer_12_out1, demultiplexer_13_out0, demultiplexer_13_out1, demultiplexer_16_out0,
       demultiplexer_16_out1, demultiplexer_17_out0, demultiplexer_17_out1, demultiplexer_18_out0,
       demultiplexer_18_out1, demultiplexer_20_out0, demultiplexer_21_out0, demultiplexer_21_out1,
       demultiplexer_22_out0, demultiplexer_22_out1, demultiplexer_23_out0, demultiplexer_23_out1,
       demultiplexer_24_out0, demultiplexer_24_out1, demultiplexer_26_out0, Itype, LoadItype, Rtype;

  Demultiplexer demultiplexer_1 (
    .out0(demultiplexer_1_out0), .out1(demultiplexer_1_out1), .in(1'b1), .sel(Instruction[6]));  // open: en
  Demultiplexer demultiplexer_2 (
    .out0(demultiplexer_2_out0), .out1(JALtype), .in(demultiplexer_1_out1), .sel(Instruction[3]));  // open: en
  Demultiplexer demultiplexer_3 (
    .out0(demultiplexer_3_out0), .out1(Itype), .in(demultiplexer_4_out0), .sel(Instruction[4]));  // open: en
  Demultiplexer demultiplexer_4 (
    .out0(demultiplexer_4_out0), .out1(demultiplexer_4_out1), .in(demultiplexer_1_out0), .sel(Instruction[5]));  // open: en
  Demultiplexer demultiplexer_5 (
    .out0(SWtype), .out1(demultiplexer_5_out1), .in(demultiplexer_4_out1), .sel(Instruction[4]));  // open: en
  Demultiplexer demultiplexer_6 (
    .out0(demultiplexer_6_out0), .out1(JALRtype), .in(demultiplexer_2_out0), .sel(Instruction[2]));  // open: en
  Demultiplexer demultiplexer_7 (
    .out0(Rtype), .out1(LUItype), .in(demultiplexer_5_out1), .sel(Instruction[2]));  // open: en
  Demultiplexer demultiplexer_8 (.out1(LoadItype), .in(demultiplexer_3_out0), .sel(Instruction[1]));  // open: out0, en
  Demultiplexer demultiplexer_9 (
    .out0(BEQtype), .out1(demultiplexer_9_out1), .in(demultiplexer_6_out0), .sel(Instruction[14]));  // open: en
  Demultiplexer demultiplexer_10 (
    .out0(BLTtype), .out1(BLTUtype), .in(demultiplexer_9_out1), .sel(Instruction[13]));  // open: en
  Demultiplexer demultiplexer_11 (
    .out0(demultiplexer_11_out0), .out1(demultiplexer_11_out1), .in(demultiplexer_12_out0),
    .sel(Instruction[13]));  // open: en
  Demultiplexer demultiplexer_12 (
    .out0(demultiplexer_12_out0), .out1(demultiplexer_12_out1), .in(Itype), .sel(Instruction[14]));  // open: en
  Demultiplexer demultiplexer_13 (
    .out0(demultiplexer_13_out0), .out1(demultiplexer_13_out1), .in(demultiplexer_12_out1),
    .sel(Instruction[13]));  // open: en
  Demultiplexer demultiplexer_14 (
    .out0(ADDItype), .out1(SLLItype), .in(demultiplexer_11_out0), .sel(Instruction[12]));  // open: en
  Demultiplexer demultiplexer_15 (
    .out0(XORItype), .out1(SRLItype), .in(demultiplexer_13_out0), .sel(Instruction[12]));  // open: en
  Demultiplexer demultiplexer_16 (
    .out0(demultiplexer_16_out0), .out1(demultiplexer_16_out1), .in(demultiplexer_17_out0),
    .sel(Instruction[13]));  // open: en
  Demultiplexer demultiplexer_17 (
    .out0(demultiplexer_17_out0), .out1(demultiplexer_17_out1), .in(Rtype), .sel(Instruction[14]));  // open: en
  Demultiplexer demultiplexer_18 (
    .out0(demultiplexer_18_out0), .out1(demultiplexer_18_out1), .in(demultiplexer_17_out1),
    .sel(Instruction[13]));  // open: en
  Demultiplexer demultiplexer_19 (
    .out0(SLTItype), .in(demultiplexer_11_out1), .sel(Instruction[12]));  // open: out1, en
  Demultiplexer demultiplexer_20 (
    .out0(demultiplexer_20_out0), .out1(LWtype), .in(LoadItype), .sel(Instruction[13]));  // open: en
  Demultiplexer demultiplexer_21 (
    .out0(demultiplexer_21_out0), .out1(demultiplexer_21_out1), .in(demultiplexer_16_out0),
    .sel(Instruction[12]));  // open: en
  Demultiplexer demultiplexer_22 (
    .out0(demultiplexer_22_out0), .out1(demultiplexer_22_out1), .in(demultiplexer_16_out1),
    .sel(Instruction[12]));  // open: en
  Demultiplexer demultiplexer_23 (
    .out0(demultiplexer_23_out0), .out1(demultiplexer_23_out1), .in(demultiplexer_18_out0),
    .sel(Instruction[12]));  // open: en
  Demultiplexer demultiplexer_24 (
    .out0(demultiplexer_24_out0), .out1(demultiplexer_24_out1), .in(demultiplexer_18_out1),
    .sel(Instruction[12]));  // open: en
  Demultiplexer demultiplexer_25 (
    .out0(ORItype), .out1(ANDItype), .in(demultiplexer_13_out1), .sel(Instruction[12]));  // open: en
  Demultiplexer demultiplexer_26 (
    .out0(demultiplexer_26_out0), .out1(SUBtype), .in(demultiplexer_21_out0), .sel(Instruction[30]));  // open: en
  Demultiplexer demultiplexer_27 (
    .out0(SLLtype), .out1(MULHtype), .in(demultiplexer_21_out1), .sel(Instruction[25]));  // open: en
  Demultiplexer demultiplexer_28 (.out0(SLTtype), .in(demultiplexer_22_out0), .sel(Instruction[25]));  // open: out1, en
  Demultiplexer demultiplexer_29 (.in(demultiplexer_22_out1), .sel(Instruction[25]));  // open: out0, out1, en
  Demultiplexer demultiplexer_30 (
    .out0(XORtype), .out1(DIVtype), .in(demultiplexer_23_out0), .sel(Instruction[25]));  // open: en
  Demultiplexer demultiplexer_31 (.out0(SRLtype), .in(demultiplexer_23_out1), .sel(Instruction[25]));  // open: out1, en
  Demultiplexer demultiplexer_32 (
    .out0(ORtype), .out1(REMtype), .in(demultiplexer_24_out0), .sel(Instruction[25]));  // open: en
  Demultiplexer demultiplexer_33 (.out0(ANDtype), .in(demultiplexer_24_out1), .sel(Instruction[25]));  // open: out1, en
  Demultiplexer demultiplexer_34 (
    .out0(LBtype), .out1(LHtype), .in(demultiplexer_20_out0), .sel(Instruction[12]));  // open: en
  Demultiplexer demultiplexer_35 (
    .out0(ADDtype), .out1(MULtype), .in(demultiplexer_26_out0), .sel(Instruction[25]));  // open: en

  assign brEQ_2 = brEQ;
  assign brLT_2 = brLT;

  // Other names for the same wires on the sheet: Op1 = Instruction[1]; Op2 = Instruction[2]; Op3 = Instruction[3];
  //   Op4 = Instruction[4]; Op5 = Instruction[5]; Op6 = Instruction[6]; Func3_12 = Instruction[12];
  //   Func3_13 = Instruction[13]; Func3_14 = Instruction[14]; Func7_25 = Instruction[25]; Func7_30 = Instruction[30]

  // Notes on the sheet:
  //   ITypes
  //   UJTypes
  //   UTypes
  //   SBTypes
  //   STypes
  //   ITypes
  //   RTypes
endmodule
